# Fritzing sketch Circuit Diagram - Fritzing (saved by Fritzing 0.9.3b)
breadboards: 1

parts:
  Part2 = u-blox NEO-6M GPS Breakout
  LM2596_-_4_1V_O/P = LM2596 step down module
  SIM800L_BO1 = SIM800L BO
  R1 = Resistor [tolerance=±10% resistance=10k package=THT]
  R2 = Resistor [tolerance=±10% resistance=20k package=THT]
  Arduino_Pro_mini = Arduino Pro Mini v13
  7805_IC = Voltage Regulator [package=to220-igo]
  D1 = Zener Diode [part_number=1N4732A breakdown_voltage=3.6V package="300 mil [THT]"]
  D2 = Diode [package=diode-1n4001]  # not connected
  C2 = Capacitor Polarized [package=cpol-radial-100uf-25v]
  C6 = Electrolytic Capacitor [capacitance=100μF package="0807 [SMD, electrolytic]"]
  C7 = Electrolytic Capacitor [capacitance=1000μF package="1010 [SMD, electrolytic]"]
  C8 = Electrolytic Capacitor [capacitance=1000μF package="1010 [SMD, electrolytic]"]
  LDR = Photocell (LDR) [package=THT]
  R4 = Resistor [tolerance=±5% resistance=10k package=THT]
  SOS_Button = SWITCH-MOMENTARY-2 [package=tactile-pth-12mm]
  2500_mAh_11_1_V_Battery = LIPO-2000mAh [package=lipo-2000]
  TP1 = TP4056 [chip_label=TP4056 package="DIP (Dual Inline) [THT]"]
  Solar_Cell = Solar Cell
  U1 = COPERNICUS-DIP [package=copernicus-dip]
  U3 = ESP8266-01S [part_number=ESP8266]

nets:
  GND: Part2.GND, LM2596_-_4_1V_O/P.IN-, LM2596_-_4_1V_O/P.OUT-, SIM800L_BO1.pin_6, R2.Pin_0, Arduino_Pro_mini.GND, 7805_IC.IN, D1.anode, C2.+, C6.-, C7.-, C8.-, R4.Pin_0, TP1.pin6
  N1: Part2.VCC, Arduino_Pro_mini.RAW, 7805_IC.OUT, LDR.pin_0
  N2: Part2.TXD, Arduino_Pro_mini.D1/RX, U1.BOOT
  N3: LM2596_-_4_1V_O/P.IN+, D1.cathode, TP1.pin3, U1.LNA, U3.VCC
  N4: LM2596_-_4_1V_O/P.OUT+, SIM800L_BO1.PIN2, C6.+, C7.+, C8.+
  N5: SIM800L_BO1.pin_4, R1.Pin_1, R2.Pin_1
  N6: SIM800L_BO1.pin_5, Arduino_Pro_mini.D2
  N7: Arduino_Pro_mini.D0/TX, U1.RESERVED2
  N8: Arduino_Pro_mini.A0, LDR.pin_1, R4.Pin_1
  N9: Arduino_Pro_mini.D11_PWM/MOSI, SOS_Button.1
  N10: 7805_IC.GND, C2.-
  N11: 2500_mAh_11_1_V_Battery.+, TP1.pin4
  N12: 2500_mAh_11_1_V_Battery.-, TP1.pin5
  N13: TP1.pin1, Solar_Cell.+
  N14: TP1.pin2, Solar_Cell.-

notes:
  Vessel Battery
  + -

custom parts:
  LM2596 step down module: LM2596 DC-DC step down power supply module 3 A.
  TP4056: A DIP stand-in part for whatever IC you want. With 6 pins on a 300mil dual inline package (DIP) footprint.
